# Fritzing sketch Is It Moist (saved by Fritzing 0.9.3b)
breadboards: 1

parts:
  IC1 = MCP3008 8-channel 10-bit ADC [part_number=MCP3008]
  Raspberry_Pi_1 = Raspberry Pi 3 [part_number=RPI-3-V1.2]
  Part2 = FC-28 Soil Hygrometer Module - Probe
  Part3 = FC-28 Soil Hygrometer Module

nets:
  N1: IC1.no_name_yet#1, Part3.AO
  GND: IC1.no_name_yet#9, IC1.no_name_yet#14, Raspberry_Pi_1.GND, Part3.GND
  N2: IC1.no_name_yet#10, Raspberry_Pi_1.GIPO8
  N3: IC1.no_name_yet#11, Raspberry_Pi_1.GIPO10
  N4: IC1.no_name_yet#12, Raspberry_Pi_1.GIPO9
  N5: IC1.no_name_yet#13, Raspberry_Pi_1.GIPO11
  3V3: IC1.no_name_yet#15, IC1.no_name_yet#16, Raspberry_Pi_1.3v3, Part3.VCC
  N6: Part2.POS, Part3.POS
  N7: Part2.NEG, Part3.NEG

custom parts:
  FC-28 Soil Hygrometer Module - Probe: The FC-28 is a soil hygrometer module that uses the Texas Instruments LM393 comparator chip to provide an analog measurement of soil humidity.
  FC-28 Soil Hygrometer Module: The FC-28 is a soil hygrometer module that uses the Texas Instruments LM393 comparator chip to provide an analog measurement of soil humidity. The digital output is high when soil moisture is over a certain threshold, as determined by adjusting the potentiometer.
